// Logisim project ece649_Fall2024_Final.circ as structural Verilog: 1 circuit, main circuit main
module main (
  input  rst,
  input  in_2,
  output [4:0] out_3,
  output [31:0] out_4,
  output [31:0] out_5,
  output [7:0] out_6,
  output [7:0] out_7
);

  wire and_1_out, and_2_out, and_3_out, and_4_out, clock_1_out, comparator_1_eq, comparator_2_eq,
       comparator_3_eq, comparator_4_eq, comparator_5_eq, comparator_6_eq, comparator_7_eq, comparator_8_eq,
       comparator_9_eq, comparator_10_eq, comparator_11_gt, decoder_1_out0, decoder_1_out1, decoder_1_out2,
       decoder_1_out3, decoder_1_out4, decoder_1_out5, decoder_1_out6, decoder_1_out7, decoder_1_out8,
       decoder_1_out9, decoder_1_out10, decoder_1_out11, decoder_1_out12, decoder_1_out13, decoder_1_out14,
       decoder_1_out15, decoder_1_out16, decoder_1_out17, decoder_1_out18, decoder_1_out19, decoder_1_out20,
       decoder_1_out21, decoder_1_out22, decoder_1_out23, decoder_1_out24, decoder_1_out25, decoder_1_out26,
       decoder_1_out27, decoder_1_out28, decoder_1_out29, decoder_1_out30, decoder_1_out31, decoder_2_out0,
       decoder_2_out4, decoder_2_out8, decoder_2_out12, decoder_2_out24, not_2_out, not_3_out, not_4_out,
       or_1_out;
  wire [3:0] ram_1_dout_2;
  wire [7:0] adder_1_out, multiplexer_1_out, ProgramC_q;
  wire [9:0] bit_extender_3_out, c0_q, c1_q, c2_q, c3_q, c4_q, c5_q, c6_q, c7_q, c8_q, c9_q,
       multiplexer_3_out, multiplexer_4_out, multiplexer_5_out, multiplexer_6_out, multiplexer_7_out,
       multiplexer_8_out, multiplexer_9_out, multiplexer_10_out, multiplexer_11_out, multiplexer_12_out;
  wire [24:0] ram_1_dout;
  wire [31:0] adder_3_out, adder_4_out, bit_extender_1_out, bit_extender_2_out, multiplexer_2_out,
       multiplexer_14_out, multiplexer_15_out, multiplexer_17_out, not_1_out, ram_2_dout, x0_q, x1_q, x2_q,
       x3_q, x4_q, x5_q, x6_q, x7_q, x8_q, x10_q, x11_q, x12_q, x13_q, x14_q, x15_q, x16_q, x17_q, x18_q,
       x19_q, x20_q, x21_q, x22_q, x23_q, x24_q, x25_q, x26_q, x27_q, x28_q, x29_q, x30_q, x31_q, x32_q;
  wire [31:8] adder_2_out;

  Clock clock_1 (.out(clock_1_out));
  Register ProgramC (.D(adder_1_out), .en(1'b1), .clk(clock_1_out), .Q(ProgramC_q), .clr(rst));
  RAM #(.dataWidth(32)) ram_1 (
    .addr(ProgramC_q), .we(1'b0), .oe(1'b1), .clk(clock_1_out),
    .dout({ram_1_dout_2, out_6[7:5], ram_1_dout[24:12], out_6[4:1], ram_1_dout[7], out_3, ram_1_dout[1:0]}));  // open: din
  RAM #(.dataWidth(32)) ram_2 (
    .addr(out_7), .we(decoder_2_out8), .oe(1'b1), .clk(clock_1_out), .din(multiplexer_14_out),
    .dout(ram_2_dout));
  Multiplexer #(.width(8)) multiplexer_1 (
    .in0(8'h1), .in1({out_6[7:1], 1'b0}), .out(multiplexer_1_out), .sel(and_2_out));
  Adder adder_1 (.a(ProgramC_q), .b(multiplexer_1_out), .out(adder_1_out));  // open: cin, cout
  assign bit_extender_1_out = {{20{ram_1_dout_2[3]}}, {ram_1_dout_2, out_6[7:1], ram_1_dout[7]}};  // Bit_Extender bit_extender_1
  assign bit_extender_2_out = {{20{ram_1_dout_2[3]}}, {ram_1_dout_2, out_6[7:5], ram_1_dout[24:20]}};  // Bit_Extender bit_extender_2
  Decoder #(.select(5)) decoder_1 (
    .out0(decoder_1_out0), .out1(decoder_1_out1), .out2(decoder_1_out2), .out3(decoder_1_out3),
    .out4(decoder_1_out4), .out5(decoder_1_out5), .out6(decoder_1_out6), .out7(decoder_1_out7),
    .out8(decoder_1_out8), .out9(decoder_1_out9), .out10(decoder_1_out10), .out11(decoder_1_out11),
    .out12(decoder_1_out12), .out13(decoder_1_out13), .out14(decoder_1_out14), .out15(decoder_1_out15),
    .out16(decoder_1_out16), .out17(decoder_1_out17), .out18(decoder_1_out18), .out19(decoder_1_out19),
    .out20(decoder_1_out20), .out21(decoder_1_out21), .out22(decoder_1_out22), .out23(decoder_1_out23),
    .out24(decoder_1_out24), .out25(decoder_1_out25), .out26(decoder_1_out26), .out27(decoder_1_out27),
    .out28(decoder_1_out28), .out29(decoder_1_out29), .out30(decoder_1_out30), .out31(decoder_1_out31),
    .sel({out_6[4:1], ram_1_dout[7]}), .en(and_3_out));
  Multiplexer #(.width(32)) multiplexer_2 (
    .in0(bit_extender_1_out), .in1(bit_extender_2_out), .out(multiplexer_2_out), .sel(decoder_2_out0));
  Bit_Extender #(.in_width(32), .out_width(10)) bit_extender_3 (.in(multiplexer_14_out), .out(bit_extender_3_out));
  Adder #(.width(32)) adder_2 (.a(out_4), .b(multiplexer_2_out), .out({adder_2_out, out_7}));  // open: cin, cout
  Register #(.width(32)) x0 (.D(multiplexer_17_out), .en(1'b0), .clk(clock_1_out), .Q(x0_q), .clr(rst));
  Register #(.width(32)) x1 (.D(multiplexer_17_out), .en(decoder_1_out1), .clk(clock_1_out), .Q(x1_q), .clr(rst));
  Register #(.width(32)) x2 (.D(multiplexer_17_out), .en(decoder_1_out2), .clk(clock_1_out), .Q(x2_q), .clr(rst));
  Register #(.width(32)) x3 (.D(multiplexer_17_out), .en(decoder_1_out3), .clk(clock_1_out), .Q(x3_q), .clr(rst));
  Register #(.width(32)) x4 (.D(multiplexer_17_out), .en(decoder_1_out4), .clk(clock_1_out), .Q(x4_q), .clr(rst));
  Register #(.width(32)) x5 (.D(multiplexer_17_out), .en(decoder_1_out5), .clk(clock_1_out), .Q(x5_q), .clr(rst));
  Register #(.width(32)) x6 (.D(multiplexer_17_out), .en(decoder_1_out6), .clk(clock_1_out), .Q(x6_q), .clr(rst));
  Register #(.width(32)) x7 (.D(multiplexer_17_out), .en(decoder_1_out7), .clk(clock_1_out), .Q(x7_q), .clr(rst));
  Comparator #(.mode("unsigned")) comparator_1 (.a(out_7), .b(8'h50), .eq(comparator_1_eq));  // open: gt, lt
  Comparator #(.mode("unsigned")) comparator_2 (.a(out_7), .b(8'h54), .eq(comparator_2_eq));  // open: gt, lt
  Comparator #(.mode("unsigned")) comparator_3 (.a(out_7), .b(8'h58), .eq(comparator_3_eq));  // open: gt, lt
  Comparator #(.mode("unsigned")) comparator_4 (.a(out_7), .b(8'h5c), .eq(comparator_4_eq));  // open: gt, lt
  Comparator #(.mode("unsigned")) comparator_5 (.a(out_7), .b(8'h60), .eq(comparator_5_eq));  // open: gt, lt
  Comparator #(.mode("unsigned")) comparator_6 (.a(out_7), .b(8'h64), .eq(comparator_6_eq));  // open: gt, lt
  Comparator #(.mode("unsigned")) comparator_7 (.a(out_7), .b(8'h68), .eq(comparator_7_eq));  // open: gt, lt
  Comparator #(.mode("unsigned")) comparator_8 (.a(out_7), .b(8'h6c), .eq(comparator_8_eq));  // open: gt, lt
  Comparator #(.mode("unsigned")) comparator_9 (.a(out_7), .b(8'h70), .eq(comparator_9_eq));  // open: gt, lt
  Comparator #(.mode("unsigned")) comparator_10 (.a(out_7), .b(8'h74), .eq(comparator_10_eq));  // open: gt, lt
  Register #(.width(32)) x8 (.en(decoder_1_out8), .clk(clock_1_out), .Q(x8_q), .clr(rst));  // open: D
  Register #(.width(32)) x10 (.D(multiplexer_17_out), .en(decoder_1_out9), .clk(clock_1_out), .Q(x10_q), .clr(rst));
  Register #(.width(32)) x11 (.D(multiplexer_17_out), .en(decoder_1_out10), .clk(clock_1_out), .Q(x11_q), .clr(rst));
  Register #(.width(32)) x12 (.D(multiplexer_17_out), .en(decoder_1_out11), .clk(clock_1_out), .Q(x12_q), .clr(rst));
  Register #(.width(32)) x13 (.D(multiplexer_17_out), .en(decoder_1_out12), .clk(clock_1_out), .Q(x13_q), .clr(rst));
  Register #(.width(32)) x14 (.D(multiplexer_17_out), .en(decoder_1_out13), .clk(clock_1_out), .Q(x14_q), .clr(rst));
  Register #(.width(32)) x15 (.D(multiplexer_17_out), .en(decoder_1_out14), .clk(clock_1_out), .Q(x15_q), .clr(rst));
  Register #(.width(32)) x16 (.D(multiplexer_17_out), .en(decoder_1_out15), .clk(clock_1_out), .Q(x16_q), .clr(rst));
  Register #(.width(32)) x17 (.en(decoder_1_out16), .clk(clock_1_out), .Q(x17_q), .clr(rst));  // open: D
  Register #(.width(32)) x18 (.en(decoder_1_out17), .clk(clock_1_out), .Q(x18_q), .clr(rst));  // open: D
  Register #(.width(32)) x19 (.en(decoder_1_out18), .clk(clock_1_out), .Q(x19_q), .clr(rst));  // open: D
  Register #(.width(32)) x20 (.en(decoder_1_out19), .clk(clock_1_out), .Q(x20_q), .clr(rst));  // open: D
  Register #(.width(32)) x21 (.en(decoder_1_out20), .clk(clock_1_out), .Q(x21_q), .clr(rst));  // open: D
  Register #(.width(32)) x22 (.en(decoder_1_out21), .clk(clock_1_out), .Q(x22_q), .clr(rst));  // open: D
  Register #(.width(32)) x23 (.en(decoder_1_out22), .clk(clock_1_out), .Q(x23_q), .clr(rst));  // open: D
  Register #(.width(32)) x24 (.en(decoder_1_out23), .clk(clock_1_out), .Q(x24_q), .clr(rst));  // open: D
  Register #(.width(10)) c0 (.D(bit_extender_3_out), .en(comparator_1_eq), .clk(clock_1_out), .Q(c0_q), .clr(rst));
  Register #(.width(10)) c1 (.D(bit_extender_3_out), .en(comparator_2_eq), .clk(clock_1_out), .Q(c1_q), .clr(rst));
  Register #(.width(10)) c2 (.D(bit_extender_3_out), .en(comparator_3_eq), .clk(clock_1_out), .Q(c2_q), .clr(rst));
  Register #(.width(10)) c3 (.D(bit_extender_3_out), .en(comparator_4_eq), .clk(clock_1_out), .Q(c3_q), .clr(rst));
  Register #(.width(10)) c4 (.D(bit_extender_3_out), .en(comparator_5_eq), .clk(clock_1_out), .Q(c4_q), .clr(rst));
  Register #(.width(10)) c5 (.D(bit_extender_3_out), .en(comparator_6_eq), .clk(clock_1_out), .Q(c5_q), .clr(rst));
  Register #(.width(10)) c6 (.D(bit_extender_3_out), .en(comparator_7_eq), .clk(clock_1_out), .Q(c6_q), .clr(rst));
  Register #(.width(10)) c7 (.D(bit_extender_3_out), .en(comparator_8_eq), .clk(clock_1_out), .Q(c7_q), .clr(rst));
  Register #(.width(10)) c8 (.D(bit_extender_3_out), .en(comparator_9_eq), .clk(clock_1_out), .Q(c8_q), .clr(rst));
  Register #(.width(10)) c9 (.D(bit_extender_3_out), .en(comparator_10_eq), .clk(clock_1_out), .Q(c9_q), .clr(rst));
  Register #(.width(32)) x25 (.en(decoder_1_out24), .clk(clock_1_out), .Q(x25_q), .clr(rst));  // open: D
  Register #(.width(32)) x26 (.en(decoder_1_out25), .clk(clock_1_out), .Q(x26_q), .clr(rst));  // open: D
  Register #(.width(32)) x27 (.en(decoder_1_out26), .Q(x27_q), .clr(rst));  // open: D, clk
  Register #(.width(32)) x28 (.en(decoder_1_out27), .clk(clock_1_out), .Q(x28_q), .clr(rst));  // open: D
  Register #(.width(32)) x29 (.en(decoder_1_out28), .clk(clock_1_out), .Q(x29_q), .clr(rst));  // open: D
  Register #(.width(32)) x30 (.en(decoder_1_out29), .clk(clock_1_out), .Q(x30_q), .clr(rst));  // open: D
  Register #(.width(32)) x31 (.en(decoder_1_out30), .clk(clock_1_out), .Q(x31_q), .clr(rst));  // open: D
  Register #(.width(32)) x32 (.en(decoder_1_out31), .clk(clock_1_out), .Q(x32_q), .clr(rst));  // open: D
  Multiplexer #(.width(10)) multiplexer_3 (.in0({10{1'b0}}), .in1(c0_q), .out(multiplexer_3_out), .sel(in_2));
  Multiplexer #(.width(10)) multiplexer_4 (.in0(10'h18), .in1(c1_q), .out(multiplexer_4_out), .sel(in_2));
  Multiplexer #(.width(10)) multiplexer_5 (.in0(10'h4), .in1(c2_q), .out(multiplexer_5_out), .sel(in_2));
  Multiplexer #(.width(10)) multiplexer_6 (.in0(10'h1c2), .in1(c3_q), .out(multiplexer_6_out), .sel(in_2));
  Multiplexer #(.width(10)) multiplexer_7 (.in0(10'h2), .in1(c4_q), .out(multiplexer_7_out), .sel(in_2));
  Multiplexer #(.width(10)) multiplexer_8 (.in0(10'h2), .in1(c5_q), .out(multiplexer_8_out), .sel(in_2));
  Multiplexer #(.width(10)) multiplexer_9 (.in0(10'h1c2), .in1(c6_q), .out(multiplexer_9_out), .sel(in_2));
  Multiplexer #(.width(10)) multiplexer_10 (.in0(10'h4), .in1(c7_q), .out(multiplexer_10_out), .sel(in_2));
  Multiplexer #(.width(10)) multiplexer_11 (.in0(10'h18), .in1(c8_q), .out(multiplexer_11_out), .sel(in_2));
  Multiplexer #(.width(10)) multiplexer_12 (.in0({10{1'b0}}), .in1(c9_q), .out(multiplexer_12_out), .sel(in_2));
  DotMatrix #(.matrixcols(10), .matrixrows(10)) dotmatrix_1 (
    .col0(multiplexer_3_out), .col1(multiplexer_4_out), .col2(multiplexer_5_out), .col3(multiplexer_6_out),
    .col4(multiplexer_7_out), .col5(multiplexer_8_out), .col6(multiplexer_9_out), .col7(multiplexer_10_out),
    .col8(multiplexer_11_out), .col9(multiplexer_12_out));
  Multiplexer #(.select(5), .width(32)) multiplexer_13 (
    .in0(x0_q), .in1(x1_q), .in2(x2_q), .in3(x3_q), .in4(x4_q), .in5(x5_q), .in6(x6_q), .in7(x7_q),
    .in8(x8_q), .in9(x10_q), .in10(x11_q), .in11(x12_q), .in12(x13_q), .in13(x14_q), .in14(x15_q),
    .in15(x16_q), .in16(x17_q), .in17(x18_q), .in18(x19_q), .in19(x20_q), .in20(x21_q), .in21(x22_q),
    .in22(x23_q), .in23(x24_q), .in24(x25_q), .in25(x26_q), .in26(x27_q), .in27(x28_q), .in28(x29_q),
    .in29(x30_q), .in30(x31_q), .in31(x32_q), .out(out_4), .sel(ram_1_dout[19:15]));
  Multiplexer #(.select(5), .width(32)) multiplexer_14 (
    .in0(x0_q), .in1(x1_q), .in2(x2_q), .in3(x3_q), .in4(x4_q), .in5(x5_q), .in6(x6_q), .in7(x7_q),
    .in8(x8_q), .in9(x10_q), .in10(x11_q), .in11(x12_q), .in12(x13_q), .in13(x14_q), .in14(x15_q),
    .in15(x16_q), .in16(x17_q), .in17(x18_q), .in18(x19_q), .in19(x20_q), .in20(x21_q), .in21(x22_q),
    .in22(x23_q), .in23(x24_q), .in24(x25_q), .in25(x26_q), .in26(x27_q), .in27(x28_q), .in28(x29_q),
    .in29(x30_q), .in30(x31_q), .in31(x32_q), .out(multiplexer_14_out), .sel(ram_1_dout[24:20]));
  Multiplexer #(.width(32)) multiplexer_15 (
    .in0(multiplexer_14_out), .in1(bit_extender_2_out), .out(multiplexer_15_out), .sel(decoder_2_out4));
  assign not_1_out = ~multiplexer_15_out;  // NOT_Gate not_1, 32 bits wide
  Adder #(.width(32)) adder_3 (.a(not_1_out), .b(32'h1), .out(adder_3_out));  // open: cin, cout
  or or_1 (or_1_out, and_1_out, decoder_2_out24);
  and and_1 (and_1_out, ram_1_dout_2[2], decoder_2_out12);
  Adder #(.width(32)) adder_4 (.a(out_4), .b(out_5), .out(adder_4_out));  // open: cin, cout
  Multiplexer #(.width(32)) multiplexer_16 (.in0(multiplexer_15_out), .in1(adder_3_out), .out(out_5), .sel(or_1_out));
  Multiplexer #(.width(32)) multiplexer_17 (
    .in0(adder_4_out), .in1(ram_2_dout), .out(multiplexer_17_out), .sel(decoder_2_out0));
  and and_2 (and_2_out, decoder_2_out24, and_4_out);
  and and_3 (and_3_out, not_2_out, not_3_out);
  and and_4 (and_4_out, 1'b1, not_4_out);
  not not_2 (not_2_out, decoder_2_out24);
  not not_3 (not_3_out, decoder_2_out8);
  not not_4 (not_4_out, comparator_11_gt);
  Decoder #(.select(5)) decoder_2 (
    .out0(decoder_2_out0), .out4(decoder_2_out4), .out8(decoder_2_out8), .out12(decoder_2_out12),
    .out24(decoder_2_out24), .sel(out_3), .en(1'b1));  // open: out1, out2, out3, out5, out6, out7, out9, out10, out11, out13, out14, out15, out16, out17, out18, out19, out20, out21, out22, out23, out25, out26, out27, out28, out29, out30, out31
  Comparator #(.mode("unsigned"), .width(32)) comparator_11 (
    .a(adder_4_out), .b({32{1'b0}}), .gt(comparator_11_gt));  // open: eq, lt

  assign out_6[0] = 1'b0;

  // Notes on the sheet:
  //   Funct7
  //   Funct3
  //   rd
  //   rs1
  //   rs2
  //   rs2
  //   2nd ex
  //   opcode
  //   rs1
  //   middle
  //   clk
  //   rst
  //   Addr of c0: 0101 0000
  //   Addr of c1: 0101 0100
  //   Addr of c2: 0101 1000
  //   Addr of c3: 0101 1100
  //   Addr of c4: 0110 0000
  //   Addr of c5: 0110 0100
  //   Addr of c6: 0110 1000
  //   Addr of c7: 0110 1100
  //   Addr of c8: 0111 0000
  //   Addr of c9: 0111 0100
  //   data return
  //   mux select
  //   set decoder
  //   lw
  //   addi
  //   sw
  //   add/sub
  //   beq
  //   if is 0
endmodule
